# Fritzing sketch buss (saved by Fritzing 0.8.0b)
perfboards: 1

parts:
  J1 = Piezo Speaker
  Part1 = Arduino Uno (Rev3)  # not connected
  J2 = shrouded pin header, 10 pins [form="♂ (shrouded male)"]
  S1 = Tilt Switch [package=THT]
  R2 = Resistor [tolerance=±5% resistance=15k package=THT]
  R1 = Resistor [tolerance=±5% resistance=100 package=THT]

nets:
  N1: J1.pin2, R1.Pin_1
  N2: J2.pin5, R1.Pin_0
  N3: J2.pin10, R2.Pin_1
  N4: S1.Pin_2, R2.Pin_0
